# Fritzing sketch WBox2a (saved by Fritzing 0.9.10b)
circuit board: 10.614cm x 3.8852cm
breadboards: 1

parts:
  Mod1 = Amica NodeMCU DEVKIT 1.0
  M1 = RioRand LM2596
  J-pwr = female pin header, 2 pins [form="♀ (female)"]
  J-humidity = female alternating pin header, 4 pins [form="♀ (female)"]
  J-RG11 = female alternating pin header, 4 pins [form="♀ (female)"]
  J-skysensor = female alternating pin header, 4 pins [form="♀ (female)"]

nets:
  N1: Mod1.pin1, Mod1.pin_10, Mod1.pin_26, J-humidity.pin3, J-skysensor.pin3
  N2: Mod1.pin2, Mod1.pin_9, Mod1.pin_25, Mod1.pin_29, M1.Pin_4, J-humidity.pin4, J-RG11.pin1, J-skysensor.pin4
  N3: Mod1.pin6, J-RG11.pin2
  N4: Mod1.pin_13, J-humidity.pin2, J-skysensor.pin2
  N5: Mod1.pin_14, J-humidity.pin1, J-skysensor.pin1
  N6: Mod1.pin_30, M1.Pin_3
  N7: M1.Pin_1, J-pwr.pin1, J-RG11.pin3
  N8: M1.Pin_2, J-pwr.pin2, J-RG11.pin4

notes:
  humidi
  RG-11
  skysensor]
  pwr
  G 12V
  G 12V s com
  G 3V sd sc
  sky
  hum
  AAVSO WeatherBox2
  SGEO  2023
